// Logisim project hac_01.circ as structural Verilog: 5 circuits, main circuit hac_and
module hac_and (
  input  X1,
  input  X2,
  output Y
);

  wire nand_1_out;

  nand nand_1 (nand_1_out, X1, X2);
  nand nand_2 (Y, nand_1_out, nand_1_out);
endmodule

module hac_or (
  input  X1,
  input  X2,
  output Y
);

  wire nand_1_out, nand_2_out;

  nand nand_1 (nand_1_out, X1, X1);
  nand nand_2 (nand_2_out, X2, X2);
  nand nand_3 (Y, nand_1_out, nand_2_out);
endmodule

module hac_xor (
  input  X1,
  input  X2,
  output Y
);

  wire nand_1_out, nand_2_out, nand_3_out, nand_4_out;

  nand nand_1 (nand_1_out, X1, X1);
  nand nand_2 (nand_2_out, X2, X2);
  nand nand_3 (nand_3_out, nand_1_out, X2);
  nand nand_4 (nand_4_out, X1, nand_2_out);
  nand nand_5 (Y, nand_3_out, nand_4_out);
endmodule

module hac_mux (
  input  X1,
  input  X2,
  input  S,
  output Y
);

  wire nand_1_out, nand_2_out, nand_3_out, nand_4_out, nand_5_out, nand_6_out, nand_7_out, nand_8_out,
       nand_9_out, nand_10_out;

  nand nand_1 (nand_1_out, X1, X2);
  nand nand_2 (nand_2_out, S, nand_3_out);
  nand nand_3 (nand_3_out, S, S);
  nand nand_4 (nand_4_out, S, S);
  nand nand_5 (nand_5_out, nand_4_out, X1);
  nand nand_6 (nand_6_out, S, X2);
  nand nand_7 (nand_7_out, nand_1_out, nand_2_out);
  nand nand_8 (nand_8_out, nand_5_out, nand_6_out);
  nand nand_9 (nand_9_out, nand_7_out, nand_7_out);
  nand nand_10 (nand_10_out, nand_8_out, nand_8_out);
  nand nand_11 (Y, nand_9_out, nand_10_out);
endmodule

module hac_dmux (
  input  X,
  input  S,
  output y0,
  output y1
);

  wire nand_1_out, nand_2_out, nand_3_out;

  nand nand_1 (nand_1_out, S, S);
  nand nand_2 (nand_2_out, S, X);
  nand nand_3 (nand_3_out, X, nand_1_out);
  nand nand_4 (y0, nand_3_out, nand_3_out);
  nand nand_5 (y1, nand_2_out, nand_2_out);
endmodule
