// Logisim project hac_02.circ as structural Verilog: 4 circuits, main circuit add
module add (
  input  A,
  input  B,
  input  C_IN,
  output Y,
  output C_OUT
);

  wire and_1_out, and_2_out, xor_1_out;

  xor xor_1 (xor_1_out, A, B);
  and and_1 (and_1_out, A, B);
  xor xor_2 (Y, xor_1_out, C_IN);
  and and_2 (and_2_out, C_IN, xor_1_out);
  or or_1 (C_OUT, and_2_out, and_1_out);
endmodule

module add16 (
  input  [15:0] A16,
  input  [15:0] B16,
  output OVF,
  output [15:0] Y16
);

  wire add_2_c_out, add_3_c_out, add_4_c_out, add_5_c_out, add_6_c_out, add_7_c_out, add_8_c_out,
       add_9_c_out, add_10_c_out, add_11_c_out, add_12_c_out, add_13_c_out, add_14_c_out, add_15_c_out,
       add_16_c_out;

  add add_1 (.A(A16[15]), .B(B16[15]), .C_IN(add_2_c_out), .Y(Y16[15]), .C_OUT(OVF));
  add add_2 (.A(A16[14]), .B(B16[14]), .C_IN(add_3_c_out), .Y(Y16[14]), .C_OUT(add_2_c_out));
  add add_3 (.A(A16[13]), .B(B16[13]), .C_IN(add_4_c_out), .Y(Y16[13]), .C_OUT(add_3_c_out));
  add add_4 (.A(A16[12]), .B(B16[12]), .C_IN(add_5_c_out), .Y(Y16[12]), .C_OUT(add_4_c_out));
  add add_5 (.A(A16[11]), .B(B16[11]), .C_IN(add_6_c_out), .Y(Y16[11]), .C_OUT(add_5_c_out));
  add add_6 (.A(A16[10]), .B(B16[10]), .C_IN(add_7_c_out), .Y(Y16[10]), .C_OUT(add_6_c_out));
  add add_7 (.A(A16[9]), .B(B16[9]), .C_IN(add_8_c_out), .Y(Y16[9]), .C_OUT(add_7_c_out));
  add add_8 (.A(A16[8]), .B(B16[8]), .C_IN(add_9_c_out), .Y(Y16[8]), .C_OUT(add_8_c_out));
  add add_9 (.A(A16[7]), .B(B16[7]), .C_IN(add_10_c_out), .Y(Y16[7]), .C_OUT(add_9_c_out));
  add add_10 (.A(A16[6]), .B(B16[6]), .C_IN(add_11_c_out), .Y(Y16[6]), .C_OUT(add_10_c_out));
  add add_11 (.A(A16[5]), .B(B16[5]), .C_IN(add_12_c_out), .Y(Y16[5]), .C_OUT(add_11_c_out));
  add add_12 (.A(A16[4]), .B(B16[4]), .C_IN(add_13_c_out), .Y(Y16[4]), .C_OUT(add_12_c_out));
  add add_13 (.A(A16[3]), .B(B16[3]), .C_IN(add_14_c_out), .Y(Y16[3]), .C_OUT(add_13_c_out));
  add add_14 (.A(A16[2]), .B(B16[2]), .C_IN(add_15_c_out), .Y(Y16[2]), .C_OUT(add_14_c_out));
  add add_15 (.A(A16[1]), .B(B16[1]), .C_IN(add_16_c_out), .Y(Y16[1]), .C_OUT(add_15_c_out));
  add add_16 (.A(A16[0]), .B(B16[0]), .C_IN(1'b0), .Y(Y16[0]), .C_OUT(add_16_c_out));
endmodule

module inc16 (
  input  [15:0] A16,
  output [15:0] Y16
);

  wire and_1_out, and_2_out, and_3_out, and_4_out, and_5_out, and_6_out, and_7_out, and_8_out, and_9_out,
       and_10_out, and_11_out, and_12_out, and_13_out, and_14_out, and_15_out, not_1_out, not_2_out,
       not_3_out, not_4_out, not_5_out, not_6_out, not_7_out, not_8_out, not_9_out, not_10_out, not_11_out,
       not_12_out, not_13_out, not_14_out, not_15_out;

  xor xor_1 (Y16[15], A16[15], and_1_out);
  and and_1 (and_1_out, not_1_out, A16[14]);
  not not_1 (not_1_out, Y16[14]);
  and and_2 (and_2_out, not_2_out, A16[13]);
  not not_2 (not_2_out, Y16[13]);
  xor xor_2 (Y16[14], A16[14], and_2_out);
  not not_3 (not_3_out, Y16[12]);
  xor xor_3 (Y16[13], A16[13], and_3_out);
  and and_3 (and_3_out, not_3_out, A16[12]);
  xor xor_4 (Y16[12], A16[12], and_4_out);
  and and_4 (and_4_out, not_4_out, A16[11]);
  not not_4 (not_4_out, Y16[11]);
  xor xor_5 (Y16[11], A16[11], and_5_out);
  and and_5 (and_5_out, not_5_out, A16[10]);
  not not_5 (not_5_out, Y16[10]);
  and and_6 (and_6_out, not_6_out, A16[9]);
  not not_6 (not_6_out, Y16[9]);
  xor xor_6 (Y16[10], A16[10], and_6_out);
  not not_7 (not_7_out, Y16[8]);
  xor xor_7 (Y16[9], A16[9], and_7_out);
  and and_7 (and_7_out, not_7_out, A16[8]);
  xor xor_8 (Y16[8], A16[8], and_8_out);
  and and_8 (and_8_out, not_8_out, A16[7]);
  not not_8 (not_8_out, Y16[7]);
  xor xor_9 (Y16[7], A16[7], and_9_out);
  and and_9 (and_9_out, not_9_out, A16[6]);
  not not_9 (not_9_out, Y16[6]);
  and and_10 (and_10_out, not_10_out, A16[5]);
  not not_10 (not_10_out, Y16[5]);
  xor xor_10 (Y16[6], A16[6], and_10_out);
  not not_11 (not_11_out, Y16[4]);
  xor xor_11 (Y16[5], A16[5], and_11_out);
  and and_11 (and_11_out, not_11_out, A16[4]);
  xor xor_12 (Y16[4], A16[4], and_12_out);
  and and_12 (and_12_out, not_12_out, A16[3]);
  not not_12 (not_12_out, Y16[3]);
  xor xor_13 (Y16[3], A16[3], and_13_out);
  and and_13 (and_13_out, not_13_out, A16[2]);
  not not_13 (not_13_out, Y16[2]);
  and and_14 (and_14_out, not_14_out, A16[1]);
  not not_14 (not_14_out, Y16[1]);
  xor xor_14 (Y16[2], A16[2], and_14_out);
  not not_15 (not_15_out, Y16[0]);
  xor xor_15 (Y16[1], A16[1], and_15_out);
  and and_15 (and_15_out, not_15_out, A16[0]);
  xor xor_16 (Y16[0], A16[0], 1'b1);
endmodule

module alu (
  input  NA,
  input  ZA,
  input  [15:0] A16,
  input  NB,
  input  ZB,
  input  [15:0] B16,
  input  F,
  input  NY,
  output [15:0] Y16,
  output OVF
);

  wire [15:0] add16_1_y16, and_1_out, and_2_out, and_3_out, and_4_out, and_5_out, bit_extender_1_out,
       bit_extender_2_out, bit_extender_3_out, bit_extender_4_out, bit_extender_5_out, bit_extender_6_out,
       not_1_out, not_2_out, not_3_out, or_1_out, xor_1_out, xor_2_out;

  assign bit_extender_1_out = {{15{NA}}, NA};  // Bit_Extender bit_extender_1
  assign bit_extender_2_out = {{15{ZA}}, ZA};  // Bit_Extender bit_extender_2
  assign not_1_out = ~bit_extender_2_out;  // NOT_Gate not_1, 16 bits wide
  assign bit_extender_3_out = {{15{NB}}, NB};  // Bit_Extender bit_extender_3
  assign bit_extender_4_out = {{15{ZB}}, ZB};  // Bit_Extender bit_extender_4
  assign not_2_out = ~bit_extender_4_out;  // NOT_Gate not_2, 16 bits wide
  assign bit_extender_5_out = {{15{F}}, F};  // Bit_Extender bit_extender_5
  assign bit_extender_6_out = {{15{NY}}, NY};  // Bit_Extender bit_extender_6
  assign and_1_out = not_1_out & A16;  // AND_Gate and_1, 16 bits wide
  assign and_2_out = not_2_out & B16;  // AND_Gate and_2, 16 bits wide
  assign xor_1_out = bit_extender_1_out ^ and_1_out;  // XOR_Gate xor_1, 16 bits wide
  assign xor_2_out = bit_extender_3_out ^ and_2_out;  // XOR_Gate xor_2, 16 bits wide
  assign and_3_out = xor_1_out & xor_2_out;  // AND_Gate and_3, 16 bits wide
  add16 add16_1 (.B16(xor_2_out), .A16(xor_1_out), .OVF(OVF), .Y16(add16_1_y16));
  assign and_4_out = and_3_out & not_3_out;  // AND_Gate and_4, 16 bits wide
  assign not_3_out = ~bit_extender_5_out;  // NOT_Gate not_3, 16 bits wide
  assign and_5_out = add16_1_y16 & bit_extender_5_out;  // AND_Gate and_5, 16 bits wide
  assign or_1_out = and_4_out | and_5_out;  // OR_Gate or_1, 16 bits wide
  assign Y16 = or_1_out ^ bit_extender_6_out;  // XOR_Gate xor_3, 16 bits wide
endmodule
