// Logisim project hac_03.circ as structural Verilog
module registry_1bit (
  input  WE,
  input  D,
  output Y
);

  wire CLK_out, multiplexer_1_out, not_1_out;

  not not_1 (not_1_out, WE);
  Clock CLK (.out(CLK_out));
  D_Flip_Flop d_ff_1 (.D(multiplexer_1_out), .clk(CLK_out), .Q(Y));  // open: Qn, preset, reset
  Multiplexer multiplexer_1 (.in0(D), .in1(Y), .out(multiplexer_1_out), .sel(not_1_out));
endmodule

module registry_16bit (
  input  CLK,
  input  WE,
  input  [15:0] D16,
  output [15:0] Y16
);

  wire multiplexer_1_out, multiplexer_2_out, multiplexer_3_out, multiplexer_4_out, multiplexer_5_out,
       multiplexer_6_out, multiplexer_7_out, multiplexer_8_out, multiplexer_9_out, multiplexer_10_out,
       multiplexer_11_out, multiplexer_12_out, multiplexer_13_out, multiplexer_14_out, multiplexer_15_out,
       multiplexer_16_out, not_1_out;

  not not_1 (not_1_out, WE);
  D_Flip_Flop d_ff_1 (.D(multiplexer_1_out), .clk(CLK), .Q(Y16[0]));  // open: Qn, preset, reset
  Multiplexer multiplexer_1 (.in0(D16[0]), .in1(Y16[0]), .out(multiplexer_1_out), .sel(not_1_out));
  D_Flip_Flop d_ff_2 (.D(multiplexer_2_out), .clk(CLK), .Q(Y16[1]));  // open: Qn, preset, reset
  Multiplexer multiplexer_2 (.in0(D16[1]), .in1(Y16[1]), .out(multiplexer_2_out), .sel(not_1_out));
  D_Flip_Flop d_ff_3 (.D(multiplexer_3_out), .clk(CLK), .Q(Y16[2]));  // open: Qn, preset, reset
  Multiplexer multiplexer_3 (.in0(D16[2]), .in1(Y16[2]), .out(multiplexer_3_out), .sel(not_1_out));
  D_Flip_Flop d_ff_4 (.D(multiplexer_4_out), .clk(CLK), .Q(Y16[3]));  // open: Qn, preset, reset
  Multiplexer multiplexer_4 (.in0(D16[3]), .in1(Y16[3]), .out(multiplexer_4_out), .sel(not_1_out));
  D_Flip_Flop d_ff_5 (.D(multiplexer_5_out), .clk(CLK), .Q(Y16[4]));  // open: Qn, preset, reset
  Multiplexer multiplexer_5 (.in0(D16[4]), .in1(Y16[4]), .out(multiplexer_5_out), .sel(not_1_out));
  D_Flip_Flop d_ff_6 (.D(multiplexer_6_out), .clk(CLK), .Q(Y16[5]));  // open: Qn, preset, reset
  Multiplexer multiplexer_6 (.in0(D16[5]), .in1(Y16[5]), .out(multiplexer_6_out), .sel(not_1_out));
  D_Flip_Flop d_ff_7 (.D(multiplexer_7_out), .clk(CLK), .Q(Y16[6]));  // open: Qn, preset, reset
  Multiplexer multiplexer_7 (.in0(D16[6]), .in1(Y16[6]), .out(multiplexer_7_out), .sel(not_1_out));
  D_Flip_Flop d_ff_8 (.D(multiplexer_8_out), .clk(CLK), .Q(Y16[7]));  // open: Qn, preset, reset
  Multiplexer multiplexer_8 (.in0(D16[7]), .in1(Y16[7]), .out(multiplexer_8_out), .sel(not_1_out));
  D_Flip_Flop d_ff_9 (.D(multiplexer_9_out), .clk(CLK), .Q(Y16[8]));  // open: Qn, preset, reset
  Multiplexer multiplexer_9 (.in0(D16[8]), .in1(Y16[8]), .out(multiplexer_9_out), .sel(not_1_out));
  D_Flip_Flop d_ff_10 (.D(multiplexer_10_out), .clk(CLK), .Q(Y16[9]));  // open: Qn, preset, reset
  Multiplexer multiplexer_10 (.in0(D16[9]), .in1(Y16[9]), .out(multiplexer_10_out), .sel(not_1_out));
  D_Flip_Flop d_ff_11 (.D(multiplexer_11_out), .clk(CLK), .Q(Y16[10]));  // open: Qn, preset, reset
  Multiplexer multiplexer_11 (.in0(D16[10]), .in1(Y16[10]), .out(multiplexer_11_out), .sel(not_1_out));
  D_Flip_Flop d_ff_12 (.D(multiplexer_12_out), .clk(CLK), .Q(Y16[11]));  // open: Qn, preset, reset
  Multiplexer multiplexer_12 (.in0(D16[11]), .in1(Y16[11]), .out(multiplexer_12_out), .sel(not_1_out));
  D_Flip_Flop d_ff_13 (.D(multiplexer_13_out), .clk(CLK), .Q(Y16[12]));  // open: Qn, preset, reset
  Multiplexer multiplexer_13 (.in0(D16[12]), .in1(Y16[12]), .out(multiplexer_13_out), .sel(not_1_out));
  D_Flip_Flop d_ff_14 (.D(multiplexer_14_out), .clk(CLK), .Q(Y16[13]));  // open: Qn, preset, reset
  Multiplexer multiplexer_14 (.in0(D16[13]), .in1(Y16[13]), .out(multiplexer_14_out), .sel(not_1_out));
  D_Flip_Flop d_ff_15 (.D(multiplexer_15_out), .clk(CLK), .Q(Y16[14]));  // open: Qn, preset, reset
  Multiplexer multiplexer_15 (.in0(D16[14]), .in1(Y16[14]), .out(multiplexer_15_out), .sel(not_1_out));
  D_Flip_Flop d_ff_16 (.D(multiplexer_16_out), .clk(CLK), .Q(Y16[15]));  // open: Qn, preset, reset
  Multiplexer multiplexer_16 (.in0(D16[15]), .in1(Y16[15]), .out(multiplexer_16_out), .sel(not_1_out));
endmodule

module ram_8 (
  input  WE,
  input  CLK,
  input  [2:0] ADR,
  input  [15:0] D_IN,
  output [15:0] D_OUT
);

  wire demultiplexer_1_out0, demultiplexer_1_out1, demultiplexer_1_out2, demultiplexer_1_out3,
       demultiplexer_1_out4, demultiplexer_1_out5, demultiplexer_1_out6, demultiplexer_1_out7;
  wire [15:0] registry_16bit_1_y16, registry_16bit_2_y16, registry_16bit_3_y16, registry_16bit_4_y16,
       registry_16bit_5_y16, registry_16bit_6_y16, registry_16bit_7_y16, registry_16bit_8_y16;

  Demultiplexer #(.select(3)) demultiplexer_1 (
    .out0(demultiplexer_1_out0), .out1(demultiplexer_1_out1), .out2(demultiplexer_1_out2),
    .out3(demultiplexer_1_out3), .out4(demultiplexer_1_out4), .out5(demultiplexer_1_out5),
    .out6(demultiplexer_1_out6), .out7(demultiplexer_1_out7), .in(WE), .sel(ADR));
  registry_16bit registry_16bit_1 (.D16(D_IN), .CLK(CLK), .WE(demultiplexer_1_out0), .Y16(registry_16bit_1_y16));
  registry_16bit registry_16bit_2 (.D16(D_IN), .CLK(CLK), .WE(demultiplexer_1_out1), .Y16(registry_16bit_2_y16));
  registry_16bit registry_16bit_3 (.D16(D_IN), .CLK(CLK), .WE(demultiplexer_1_out2), .Y16(registry_16bit_3_y16));
  registry_16bit registry_16bit_4 (.D16(D_IN), .CLK(CLK), .WE(demultiplexer_1_out3), .Y16(registry_16bit_4_y16));
  registry_16bit registry_16bit_5 (.D16(D_IN), .CLK(CLK), .WE(demultiplexer_1_out4), .Y16(registry_16bit_5_y16));
  registry_16bit registry_16bit_6 (.D16(D_IN), .CLK(CLK), .WE(demultiplexer_1_out5), .Y16(registry_16bit_6_y16));
  registry_16bit registry_16bit_7 (.D16(D_IN), .CLK(CLK), .WE(demultiplexer_1_out6), .Y16(registry_16bit_7_y16));
  registry_16bit registry_16bit_8 (.D16(D_IN), .CLK(CLK), .WE(demultiplexer_1_out7), .Y16(registry_16bit_8_y16));
  Multiplexer #(.select(3), .width(16)) multiplexer_1 (
    .in0(registry_16bit_1_y16), .in1(registry_16bit_2_y16), .in2(registry_16bit_3_y16),
    .in3(registry_16bit_4_y16), .in4(registry_16bit_5_y16), .in5(registry_16bit_6_y16),
    .in6(registry_16bit_7_y16), .in7(registry_16bit_8_y16), .out(D_OUT), .sel(ADR));
endmodule

module ram_64 (
  input  CLK,
  input  WE,
  input  [5:0] ADR,
  input  [15:0] D_IN,
  output [15:0] D_OUT
);

  wire demultiplexer_1_out0, demultiplexer_1_out1, demultiplexer_1_out2, demultiplexer_1_out3,
       demultiplexer_1_out4, demultiplexer_1_out5, demultiplexer_1_out6, demultiplexer_1_out7;
  wire [15:0] ram_8_1_d_out, ram_8_2_d_out, ram_8_3_d_out, ram_8_4_d_out, ram_8_5_d_out, ram_8_6_d_out,
       ram_8_7_d_out, ram_8_8_d_out;

  Demultiplexer #(.select(3)) demultiplexer_1 (
    .out0(demultiplexer_1_out0), .out1(demultiplexer_1_out1), .out2(demultiplexer_1_out2),
    .out3(demultiplexer_1_out3), .out4(demultiplexer_1_out4), .out5(demultiplexer_1_out5),
    .out6(demultiplexer_1_out6), .out7(demultiplexer_1_out7), .in(WE), .sel(ADR[5:3]));
  ram_8 ram_8_1 (.D_IN(D_IN), .WE(demultiplexer_1_out0), .ADR(ADR[2:0]), .CLK(CLK), .D_OUT(ram_8_1_d_out));
  ram_8 ram_8_2 (.D_IN(D_IN), .WE(demultiplexer_1_out1), .ADR(ADR[2:0]), .CLK(CLK), .D_OUT(ram_8_2_d_out));
  ram_8 ram_8_3 (.D_IN(D_IN), .WE(demultiplexer_1_out2), .ADR(ADR[2:0]), .CLK(CLK), .D_OUT(ram_8_3_d_out));
  ram_8 ram_8_4 (.D_IN(D_IN), .WE(demultiplexer_1_out3), .ADR(ADR[2:0]), .CLK(CLK), .D_OUT(ram_8_4_d_out));
  ram_8 ram_8_5 (.D_IN(D_IN), .WE(demultiplexer_1_out4), .ADR(ADR[2:0]), .CLK(CLK), .D_OUT(ram_8_5_d_out));
  ram_8 ram_8_6 (.D_IN(D_IN), .WE(demultiplexer_1_out5), .ADR(ADR[2:0]), .CLK(CLK), .D_OUT(ram_8_6_d_out));
  ram_8 ram_8_7 (.D_IN(D_IN), .WE(demultiplexer_1_out6), .ADR(ADR[2:0]), .CLK(CLK), .D_OUT(ram_8_7_d_out));
  ram_8 ram_8_8 (.D_IN(D_IN), .WE(demultiplexer_1_out7), .ADR(ADR[2:0]), .CLK(CLK), .D_OUT(ram_8_8_d_out));
  Multiplexer #(.select(3), .width(16)) multiplexer_1 (
    .in0(ram_8_1_d_out), .in1(ram_8_2_d_out), .in2(ram_8_3_d_out), .in3(ram_8_4_d_out), .in4(ram_8_5_d_out),
    .in5(ram_8_6_d_out), .in6(ram_8_7_d_out), .in7(ram_8_8_d_out), .out(D_OUT), .sel(ADR[5:3]));
endmodule

module ram_512 (
  input  CLK,
  input  WE,
  input  [8:0] ADR,
  input  [15:0] D_IN,
  output [15:0] D_OUT
);

  wire demultiplexer_1_out0, demultiplexer_1_out1, demultiplexer_1_out2, demultiplexer_1_out3,
       demultiplexer_1_out4, demultiplexer_1_out5, demultiplexer_1_out6, demultiplexer_1_out7;
  wire [15:0] ram_64_1_d_out, ram_64_2_d_out, ram_64_3_d_out, ram_64_4_d_out, ram_64_5_d_out, ram_64_6_d_out,
       ram_64_7_d_out, ram_64_8_d_out;

  Demultiplexer #(.select(3)) demultiplexer_1 (
    .out0(demultiplexer_1_out0), .out1(demultiplexer_1_out1), .out2(demultiplexer_1_out2),
    .out3(demultiplexer_1_out3), .out4(demultiplexer_1_out4), .out5(demultiplexer_1_out5),
    .out6(demultiplexer_1_out6), .out7(demultiplexer_1_out7), .in(WE), .sel(ADR[8:6]));
  ram_64 ram_64_1 (.ADR(ADR[5:0]), .D_IN(D_IN), .CLK(CLK), .WE(demultiplexer_1_out0), .D_OUT(ram_64_1_d_out));
  ram_64 ram_64_2 (.ADR(ADR[5:0]), .D_IN(D_IN), .CLK(CLK), .WE(demultiplexer_1_out1), .D_OUT(ram_64_2_d_out));
  ram_64 ram_64_3 (.ADR(ADR[5:0]), .D_IN(D_IN), .CLK(CLK), .WE(demultiplexer_1_out2), .D_OUT(ram_64_3_d_out));
  ram_64 ram_64_4 (.ADR(ADR[5:0]), .D_IN(D_IN), .CLK(CLK), .WE(demultiplexer_1_out3), .D_OUT(ram_64_4_d_out));
  ram_64 ram_64_5 (.ADR(ADR[5:0]), .D_IN(D_IN), .CLK(CLK), .WE(demultiplexer_1_out4), .D_OUT(ram_64_5_d_out));
  ram_64 ram_64_6 (.ADR(ADR[5:0]), .D_IN(D_IN), .CLK(CLK), .WE(demultiplexer_1_out5), .D_OUT(ram_64_6_d_out));
  ram_64 ram_64_7 (.ADR(ADR[5:0]), .D_IN(D_IN), .CLK(CLK), .WE(demultiplexer_1_out6), .D_OUT(ram_64_7_d_out));
  ram_64 ram_64_8 (.ADR(ADR[5:0]), .D_IN(D_IN), .CLK(CLK), .WE(demultiplexer_1_out7), .D_OUT(ram_64_8_d_out));
  Multiplexer #(.select(3), .width(16)) multiplexer_1 (
    .in0(ram_64_1_d_out), .in1(ram_64_2_d_out), .in2(ram_64_3_d_out), .in3(ram_64_4_d_out),
    .in4(ram_64_5_d_out), .in5(ram_64_6_d_out), .in6(ram_64_7_d_out), .in7(ram_64_8_d_out), .out(D_OUT),
    .sel(ADR[8:6]));
endmodule

module ram_4k (
  input  CLK,
  input  WE,
  input  [11:0] ADR,
  input  [15:0] D_IN,
  output [15:0] D_OUT
);

  wire demultiplexer_1_out0, demultiplexer_1_out1, demultiplexer_1_out2, demultiplexer_1_out3,
       demultiplexer_1_out4, demultiplexer_1_out5, demultiplexer_1_out6, demultiplexer_1_out7;
  wire [15:0] ram_512_1_d_out, ram_512_2_d_out, ram_512_3_d_out, ram_512_4_d_out, ram_512_5_d_out,
       ram_512_6_d_out, ram_512_7_d_out, ram_512_8_d_out;

  Demultiplexer #(.select(3)) demultiplexer_1 (
    .out0(demultiplexer_1_out0), .out1(demultiplexer_1_out1), .out2(demultiplexer_1_out2),
    .out3(demultiplexer_1_out3), .out4(demultiplexer_1_out4), .out5(demultiplexer_1_out5),
    .out6(demultiplexer_1_out6), .out7(demultiplexer_1_out7), .in(WE), .sel(ADR[11:9]));
  ram_512 ram_512_1 (.ADR(ADR[8:0]), .D_IN(D_IN), .CLK(CLK), .WE(demultiplexer_1_out0), .D_OUT(ram_512_1_d_out));
  ram_512 ram_512_2 (.ADR(ADR[8:0]), .D_IN(D_IN), .CLK(CLK), .WE(demultiplexer_1_out1), .D_OUT(ram_512_2_d_out));
  ram_512 ram_512_3 (.ADR(ADR[8:0]), .D_IN(D_IN), .CLK(CLK), .WE(demultiplexer_1_out2), .D_OUT(ram_512_3_d_out));
  ram_512 ram_512_4 (.ADR(ADR[8:0]), .D_IN(D_IN), .CLK(CLK), .WE(demultiplexer_1_out3), .D_OUT(ram_512_4_d_out));
  ram_512 ram_512_5 (.ADR(ADR[8:0]), .D_IN(D_IN), .CLK(CLK), .WE(demultiplexer_1_out4), .D_OUT(ram_512_5_d_out));
  ram_512 ram_512_6 (.ADR(ADR[8:0]), .D_IN(D_IN), .CLK(CLK), .WE(demultiplexer_1_out5), .D_OUT(ram_512_6_d_out));
  ram_512 ram_512_7 (.ADR(ADR[8:0]), .D_IN(D_IN), .CLK(CLK), .WE(demultiplexer_1_out6), .D_OUT(ram_512_7_d_out));
  ram_512 ram_512_8 (.ADR(ADR[8:0]), .D_IN(D_IN), .CLK(CLK), .WE(demultiplexer_1_out7), .D_OUT(ram_512_8_d_out));
  Multiplexer #(.select(3), .width(16)) multiplexer_1 (
    .in0(ram_512_1_d_out), .in1(ram_512_2_d_out), .in2(ram_512_3_d_out), .in3(ram_512_4_d_out),
    .in4(ram_512_5_d_out), .in5(ram_512_6_d_out), .in6(ram_512_7_d_out), .in7(ram_512_8_d_out), .out(D_OUT),
    .sel(ADR[11:9]));
endmodule
